// Logisim project carrylookaheadCS23I1005.circ as structural Verilog: 2 circuits, main circuit main
module main (
  input  CN,
  input  X0,
  input  Y0,
  input  X1,
  input  Y1,
  input  X2,
  input  Y2,
  input  X3,
  input  Y3,
  output S0,
  output S1,
  output S2,
  output S3,
  output C3,
  output out_15,
  output out_16,
  output out_17
);

  wire and_1_out, and_2_out, and_3_out, and_4_out, and_5_out, and_6_out, and_7_out, and_8_out, and_9_out,
       and_10_out, G0_out, G1_out, G2_out, G3_out, P0_out, P1_out, P2_out, P3_out;

  and G0 (G0_out, X0, Y0);
  xor P0 (P0_out, X0, Y0);
  and and_1 (and_1_out, P0_out, CN);
  or CN0 (out_15, and_1_out, G0_out);
  xor xor_1 (S0, P0_out, CN);
  xor P1 (P1_out, X1, Y1);
  and G1 (G1_out, X1, Y1);
  xor xor_2 (S1, P1_out, out_15);
  and and_2 (and_2_out, P1_out, G0_out);
  and and_3 (and_3_out, P0_out, P1_out, CN);
  xor P2 (P2_out, X2, Y2);
  and G2 (G2_out, X2, Y2);
  xor xor_3 (S2, P2_out, out_16);
  or CN1 (out_16, G1_out, and_2_out, and_3_out);
  and and_4 (and_4_out, P2_out, G1_out);
  and and_5 (and_5_out, P2_out, P1_out, G0_out);
  and and_6 (and_6_out, P2_out, P1_out, P0_out, CN);
  xor P3 (P3_out, X3, Y3);
  and G3 (G3_out, X3, Y3);
  or CN2 (out_17, G2_out, and_4_out, and_5_out, and_6_out);
  xor xor_4 (S3, out_17, P3_out);
  and and_7 (and_7_out, P3_out, G2_out);
  and and_8 (and_8_out, P3_out, P2_out, G1_out);
  and and_9 (and_9_out, P3_out, G1_out, P0_out, G0_out);
  and and_10 (and_10_out, P3_out, G1_out, P0_out, P0_out, CN);
  or CN3 (C3, G3_out, and_7_out, and_8_out, and_9_out, and_10_out);
endmodule

module Carlock (
  input  CN,
  input  X0,
  input  Y0,
  input  X1,
  input  Y1,
  input  X2,
  input  Y2,
  input  X3,
  input  Y3,
  output S0,
  output S1,
  output S2,
  output S3,
  output C3,
  output out_15,
  output out_16,
  output out_17
);

  wire and_1_out, and_2_out, and_3_out, and_4_out, and_5_out, and_6_out, and_7_out, and_8_out, and_9_out,
       and_10_out, G0_out, G1_out, G2_out, G3_out, P0_out, P1_out, P2_out, P3_out;

  xor P0 (P0_out, X0, Y0);
  and G0 (G0_out, X0, Y0);
  and and_1 (and_1_out, P0_out, CN);
  or CN0 (out_15, and_1_out, G0_out);
  xor xor_1 (S0, P0_out, CN);
  xor P1 (P1_out, X1, Y1);
  and G1 (G1_out, X1, Y1);
  xor xor_2 (S1, P1_out, out_15);
  and and_2 (and_2_out, P1_out, G0_out);
  and and_3 (and_3_out, P0_out, P1_out, CN);
  xor P2 (P2_out, X2, Y2);
  and G2 (G2_out, X2, Y2);
  xor xor_3 (S2, P2_out, out_16);
  or CN1 (out_16, G1_out, and_2_out, and_3_out);
  and and_4 (and_4_out, P2_out, G1_out);
  and and_5 (and_5_out, P2_out, P1_out, G0_out);
  and and_6 (and_6_out, P2_out, P1_out, P0_out, CN);
  xor P3 (P3_out, X3, Y3);
  and G3 (G3_out, X3, Y3);
  or CN2 (out_17, G2_out, and_4_out, and_5_out, and_6_out);
  xor xor_4 (S3, out_17, P3_out);
  and and_7 (and_7_out, P3_out, G2_out);
  and and_8 (and_8_out, P3_out, P2_out, G1_out);
  and and_9 (and_9_out, P3_out, G1_out, P0_out, G0_out);
  and and_10 (and_10_out, P3_out, G1_out, P0_out, P0_out, CN);
  or CN3 (C3, G3_out, and_7_out, and_8_out, and_9_out, and_10_out);
endmodule
